# Fritzing sketch us_sensor_sumobot_wiring (saved by Fritzing 0.8.7b)
breadboards: 1

parts:
  Part1 = Arduino Uno (Rev3)
  J1 = Basic Servo
  J2 = Basic Servo
  VCC1 = 4 x AAA Battery Mount
  Part2 = SRF05 Ultrasonic Rangefinder

nets:
  N1: Part1.D9_PWM, J1.pulse
  N2: Part1.D10_PWM/SS, J2.pulse
  N3: Part1.D12/MISO, Part2.Echo
  N4: Part1.D13/SCK, Part2.Trig
  GND: Part1.GND, J1.gnd, J2.gnd, VCC1.-, Part2.GND
  VCC: Part1.5V, J1.vcc, J2.vcc, VCC1.+, Part2.VCC
